# Fritzing sketch BSstat (saved by Fritzing 0.9.3b)
breadboards: 1

parts:
  WeMos_D1_Mini1 = WeMos D1 Mini
  R1 = Temperature Sensor (Thermistor) [thermistor_type=NTC package=THT]
  Part1 = 14-segment LED Alphanumeric Backpack [part_number=2157]
  ENCODER1 = Rotary Encoder with Knob
  R2 = Resistor [tolerance=±5% resistance=10k package="0402 [SMD]"]
  U1 = RELAY-SOLIDSTATE [package=relay-s108t02]
  Q1 = NPN-Transistor [package="TO92 [THT]"]
  R3 = Resistor [tolerance=±5% resistance=10k package="0402 [SMD]"]
  R4 = Resistor [tolerance=±5% resistance=10k package="0402 [SMD]"]
  R5 = Resistor [tolerance=±5% resistance=330 package=THT]
  J1 = female pin header, 2 pins [form="♀ (female)"]

nets:
  N1: WeMos_D1_Mini1.5V, U1.+
  N2: WeMos_D1_Mini1.A0, R1.pin_0, R2.Pin_1
  N3: WeMos_D1_Mini1.D1, Part1.SCL
  N4: WeMos_D1_Mini1.D2, Part1.SDA
  N5: WeMos_D1_Mini1.D3, ENCODER1.no_name_yet#1, R3.Pin_0
  N6: WeMos_D1_Mini1.D4, ENCODER1.no_name_yet#4
  N7: WeMos_D1_Mini1.D5, ENCODER1.no_name_yet#2, R4.Pin_0
  N8: WeMos_D1_Mini1.D7, R5.Pin_0
  GND: R1.pin_1, Part1.GND, ENCODER1.no_name_yet#3, ENCODER1.no_name_yet#5, Q1.E
  3.3V: Part1.VDD, R2.Pin_0, R3.Pin_1, R4.Pin_1
  N9: U1.T1, J1.pin1
  N10: U1.T2, J1.pin2
  N11: U1.-, Q1.C
  N12: Q1.B, R5.Pin_1

notes:
  TO FURNACE

custom parts:
  14-segment LED Alphanumeric Backpack: This is a nice, bright alphanumeric display that shows letters and numbers. It's super bright and designed for viewing from distances up to 23 feet (7 meters) away. Four digits with 14 segments on a black surface and we give you a set of two alphanumeric displays as well as a driver board so you can make a clock or a four letter word. Like our other LED backpacks, these are end-to-end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
  Rotary Encoder with Knob: Rotary Encoder with 1/4" Shaft and Knob
